# Fritzing sketch fritzing (saved by Fritzing 0.9.5d)
breadboards: 1

parts:
  U1 = NodeMCU V3.0
  LED1 = LEDs [package=led10mm]
  KY-1 = Keyes Relay [package=THT]
  Part3 = Lilypad Battery Connect

nets:
  N1: U1.D1, KY-1.signal
  N2: U1.3V3, KY-1.power
  N3: U1.GND, KY-1.ground
  N4: LED1.C, KY-1.NO
  N5: KY-1.C, Part3.+

notes:
  AC POWER SUPPLY

custom parts:
  NodeMCU V3.0: ESP8266 based NodeMCU
  LEDs: LEDs Standard schematic elements and footprints for 5mm, 3mm, 1206, and 0603 sized LEDs. 5mm - Spark Fun Electronics SKU : COM-00529 (and others)
  Keyes Relay: The Keyes 5V relay module is suitable for SCM development, home appliance control. It uses a 5V~12V TIL control signal which can control DC / AC signal.
